# Fritzing sketch photon_flash_trigger (saved by Fritzing 0.9.2b)
breadboards: 1

parts:
  Part1 = Photon
  U1 = MOC3031-M [package=dil06]
  R1 = Photocell (LDR) [package=THT]
  R2 = Resistor [tolerance=±5% resistance=220 package=THT]

nets:
  N1: Part1.A0, R1.pin_0, R2.Pin_0
  N2: Part1.A3, R1.pin_1
  N3: Part1.GND, U1.2, R2.Pin_1
  N4: Part1.D1, U1.1

notes:
  Flash pin
