# Fritzing sketch photon_shutter_release (saved by Fritzing 0.9.2b)
breadboards: 1

parts:
  Q1 = NPN-Transistor [package="TO92 [THT]"]
  Q2 = NPN-Transistor [package="TO92 [THT]"]
  R1 = Resistor [tolerance=±5% resistance=10k package=THT]
  R2 = Resistor [tolerance=±5% resistance=10k package=THT]
  Part1 = Photon

nets:
  N1: Q1.B, R1.Pin_1
  N2: Q1.C, Q2.E, Part1.GND
  N3: Q2.B, R2.Pin_1
  N4: R1.Pin_0, Part1.D3
  N5: R2.Pin_0, Part1.D1

notes:
  Ground wire
  Focus wire
  Release wire
